// Digital circuit MatrixControllerTest.dig as structural Verilog
module MatrixControllerTest (
  input  Clock,
  input  Reset,
  input  in_3,
  input  Desce_jogada,
  input  [5:0] Pontos,
  input  [2:0] Linhas_bloq,
  input  [3:0] Prox_jogada,
  input  Clock_display
);

  wire [7:0] not_1_out, not_2_out, not_3_out, u_matrix_controller_matriz_b, u_matrix_controller_matriz_col,
       u_matrix_controller_matriz_g, u_matrix_controller_matriz_r;

  matrix_controller #(.applicationType("IVERILOG")) u_matrix_controller (
    .clock(Clock), .display_refresh_clock(Clock_display), .reset_display(Reset), .show_display(in_3),
    .desce_jogada(Desce_jogada), .pontos(Pontos), .linhas_bloqueadas(Linhas_bloq), .prox_jogada(Prox_jogada),
    .matriz_col(u_matrix_controller_matriz_col), .matriz_r(u_matrix_controller_matriz_r),
    .matriz_g(u_matrix_controller_matriz_g), .matriz_b(u_matrix_controller_matriz_b));
  assign not_1_out = ~u_matrix_controller_matriz_r;  // Not not_1, 8 bits wide
  assign not_2_out = ~u_matrix_controller_matriz_b;  // Not not_2, 8 bits wide
  assign not_3_out = ~u_matrix_controller_matriz_g;  // Not not_3, 8 bits wide
  // And and_1 has open pins: In_1=not_1_out[0], In_2=u_matrix_controller_matriz_col[0], out=open
  // And and_2 has open pins: In_1=not_3_out[0], In_2=u_matrix_controller_matriz_col[0], out=open
  // And and_3 has open pins: In_1=u_matrix_controller_matriz_col[0], In_2=not_2_out[0], out=open
  // And and_4 has open pins: In_1=not_1_out[1], In_2=u_matrix_controller_matriz_col[0], out=open
  // And and_5 has open pins: In_1=not_3_out[1], In_2=u_matrix_controller_matriz_col[0], out=open
  // And and_6 has open pins: In_1=u_matrix_controller_matriz_col[0], In_2=not_2_out[1], out=open
  // And and_7 has open pins: In_1=not_1_out[2], In_2=u_matrix_controller_matriz_col[0], out=open
  // And and_8 has open pins: In_1=not_3_out[2], In_2=u_matrix_controller_matriz_col[0], out=open
  // And and_9 has open pins: In_1=u_matrix_controller_matriz_col[0], In_2=not_2_out[2], out=open
  // And and_10 has open pins: In_1=not_1_out[3], In_2=u_matrix_controller_matriz_col[0], out=open
  // And and_11 has open pins: In_1=not_3_out[3], In_2=u_matrix_controller_matriz_col[0], out=open
  // And and_12 has open pins: In_1=u_matrix_controller_matriz_col[0], In_2=not_2_out[3], out=open
  // And and_13 has open pins: In_1=not_1_out[4], In_2=u_matrix_controller_matriz_col[0], out=open
  // And and_14 has open pins: In_1=not_3_out[4], In_2=u_matrix_controller_matriz_col[0], out=open
  // And and_15 has open pins: In_1=u_matrix_controller_matriz_col[0], In_2=not_2_out[4], out=open
  // And and_16 has open pins: In_1=not_1_out[5], In_2=u_matrix_controller_matriz_col[0], out=open
  // And and_17 has open pins: In_1=not_3_out[5], In_2=u_matrix_controller_matriz_col[0], out=open
  // And and_18 has open pins: In_1=u_matrix_controller_matriz_col[0], In_2=not_2_out[5], out=open
  // And and_19 has open pins: In_1=not_1_out[6], In_2=u_matrix_controller_matriz_col[0], out=open
  // And and_20 has open pins: In_1=not_3_out[6], In_2=u_matrix_controller_matriz_col[0], out=open
  // And and_21 has open pins: In_1=u_matrix_controller_matriz_col[0], In_2=not_2_out[6], out=open
  // And and_22 has open pins: In_1=not_1_out[7], In_2=u_matrix_controller_matriz_col[0], out=open
  // And and_23 has open pins: In_1=not_3_out[7], In_2=u_matrix_controller_matriz_col[0], out=open
  // And and_24 has open pins: In_1=u_matrix_controller_matriz_col[0], In_2=not_2_out[7], out=open
  // RGBLED rgbled_1: pin names not known
  // RGBLED rgbled_2: pin names not known
  // RGBLED rgbled_3: pin names not known
  // RGBLED rgbled_4: pin names not known
  // RGBLED rgbled_5: pin names not known
  // RGBLED rgbled_6: pin names not known
  // RGBLED rgbled_7: pin names not known
  // RGBLED rgbled_8: pin names not known
  // And and_25 has open pins: In_1=not_1_out[0], In_2=u_matrix_controller_matriz_col[1], out=open
  // And and_26 has open pins: In_1=not_3_out[0], In_2=u_matrix_controller_matriz_col[1], out=open
  // And and_27 has open pins: In_1=u_matrix_controller_matriz_col[1], In_2=not_2_out[0], out=open
  // And and_28 has open pins: In_1=not_1_out[1], In_2=u_matrix_controller_matriz_col[1], out=open
  // And and_29 has open pins: In_1=not_3_out[1], In_2=u_matrix_controller_matriz_col[1], out=open
  // And and_30 has open pins: In_1=u_matrix_controller_matriz_col[1], In_2=not_2_out[1], out=open
  // And and_31 has open pins: In_1=not_1_out[2], In_2=u_matrix_controller_matriz_col[1], out=open
  // And and_32 has open pins: In_1=not_3_out[2], In_2=u_matrix_controller_matriz_col[1], out=open
  // And and_33 has open pins: In_1=u_matrix_controller_matriz_col[1], In_2=not_2_out[2], out=open
  // And and_34 has open pins: In_1=not_1_out[3], In_2=u_matrix_controller_matriz_col[1], out=open
  // And and_35 has open pins: In_1=not_3_out[3], In_2=u_matrix_controller_matriz_col[1], out=open
  // And and_36 has open pins: In_1=u_matrix_controller_matriz_col[1], In_2=not_2_out[3], out=open
  // And and_37 has open pins: In_1=not_1_out[4], In_2=u_matrix_controller_matriz_col[1], out=open
  // And and_38 has open pins: In_1=not_3_out[4], In_2=u_matrix_controller_matriz_col[1], out=open
  // And and_39 has open pins: In_1=u_matrix_controller_matriz_col[1], In_2=not_2_out[4], out=open
  // And and_40 has open pins: In_1=not_1_out[5], In_2=u_matrix_controller_matriz_col[1], out=open
  // And and_41 has open pins: In_1=not_3_out[5], In_2=u_matrix_controller_matriz_col[1], out=open
  // And and_42 has open pins: In_1=u_matrix_controller_matriz_col[1], In_2=not_2_out[5], out=open
  // And and_43 has open pins: In_1=not_1_out[6], In_2=u_matrix_controller_matriz_col[1], out=open
  // And and_44 has open pins: In_1=not_3_out[6], In_2=u_matrix_controller_matriz_col[1], out=open
  // And and_45 has open pins: In_1=u_matrix_controller_matriz_col[1], In_2=not_2_out[6], out=open
  // And and_46 has open pins: In_1=not_1_out[7], In_2=u_matrix_controller_matriz_col[1], out=open
  // And and_47 has open pins: In_1=not_3_out[7], In_2=u_matrix_controller_matriz_col[1], out=open
  // And and_48 has open pins: In_1=u_matrix_controller_matriz_col[1], In_2=not_2_out[7], out=open
  // RGBLED rgbled_9: pin names not known
  // RGBLED rgbled_10: pin names not known
  // RGBLED rgbled_11: pin names not known
  // RGBLED rgbled_12: pin names not known
  // RGBLED rgbled_13: pin names not known
  // RGBLED rgbled_14: pin names not known
  // RGBLED rgbled_15: pin names not known
  // RGBLED rgbled_16: pin names not known
  // And and_49 has open pins: In_1=not_1_out[0], In_2=u_matrix_controller_matriz_col[2], out=open
  // And and_50 has open pins: In_1=not_3_out[0], In_2=u_matrix_controller_matriz_col[2], out=open
  // And and_51 has open pins: In_1=u_matrix_controller_matriz_col[2], In_2=not_2_out[0], out=open
  // And and_52 has open pins: In_1=not_1_out[1], In_2=u_matrix_controller_matriz_col[2], out=open
  // And and_53 has open pins: In_1=not_3_out[1], In_2=u_matrix_controller_matriz_col[2], out=open
  // And and_54 has open pins: In_1=u_matrix_controller_matriz_col[2], In_2=not_2_out[1], out=open
  // And and_55 has open pins: In_1=not_1_out[2], In_2=u_matrix_controller_matriz_col[2], out=open
  // And and_56 has open pins: In_1=not_3_out[2], In_2=u_matrix_controller_matriz_col[2], out=open
  // And and_57 has open pins: In_1=u_matrix_controller_matriz_col[2], In_2=not_2_out[2], out=open
  // And and_58 has open pins: In_1=not_1_out[3], In_2=u_matrix_controller_matriz_col[2], out=open
  // And and_59 has open pins: In_1=not_3_out[3], In_2=u_matrix_controller_matriz_col[2], out=open
  // And and_60 has open pins: In_1=u_matrix_controller_matriz_col[2], In_2=not_2_out[3], out=open
  // And and_61 has open pins: In_1=not_1_out[4], In_2=u_matrix_controller_matriz_col[2], out=open
  // And and_62 has open pins: In_1=not_3_out[4], In_2=u_matrix_controller_matriz_col[2], out=open
  // And and_63 has open pins: In_1=u_matrix_controller_matriz_col[2], In_2=not_2_out[4], out=open
  // And and_64 has open pins: In_1=not_1_out[5], In_2=u_matrix_controller_matriz_col[2], out=open
  // And and_65 has open pins: In_1=not_3_out[5], In_2=u_matrix_controller_matriz_col[2], out=open
  // And and_66 has open pins: In_1=u_matrix_controller_matriz_col[2], In_2=not_2_out[5], out=open
  // And and_67 has open pins: In_1=not_1_out[6], In_2=u_matrix_controller_matriz_col[2], out=open
  // And and_68 has open pins: In_1=not_3_out[6], In_2=u_matrix_controller_matriz_col[2], out=open
  // And and_69 has open pins: In_1=u_matrix_controller_matriz_col[2], In_2=not_2_out[6], out=open
  // And and_70 has open pins: In_1=not_1_out[7], In_2=u_matrix_controller_matriz_col[2], out=open
  // And and_71 has open pins: In_1=not_3_out[7], In_2=u_matrix_controller_matriz_col[2], out=open
  // And and_72 has open pins: In_1=u_matrix_controller_matriz_col[2], In_2=not_2_out[7], out=open
  // RGBLED rgbled_17: pin names not known
  // RGBLED rgbled_18: pin names not known
  // RGBLED rgbled_19: pin names not known
  // RGBLED rgbled_20: pin names not known
  // RGBLED rgbled_21: pin names not known
  // RGBLED rgbled_22: pin names not known
  // RGBLED rgbled_23: pin names not known
  // RGBLED rgbled_24: pin names not known
  // And and_73 has open pins: In_1=not_1_out[0], In_2=u_matrix_controller_matriz_col[3], out=open
  // And and_74 has open pins: In_1=not_3_out[0], In_2=u_matrix_controller_matriz_col[3], out=open
  // And and_75 has open pins: In_1=u_matrix_controller_matriz_col[3], In_2=not_2_out[0], out=open
  // And and_76 has open pins: In_1=not_1_out[1], In_2=u_matrix_controller_matriz_col[3], out=open
  // And and_77 has open pins: In_1=not_3_out[1], In_2=u_matrix_controller_matriz_col[3], out=open
  // And and_78 has open pins: In_1=u_matrix_controller_matriz_col[3], In_2=not_2_out[1], out=open
  // And and_79 has open pins: In_1=not_1_out[2], In_2=u_matrix_controller_matriz_col[3], out=open
  // And and_80 has open pins: In_1=not_3_out[2], In_2=u_matrix_controller_matriz_col[3], out=open
  // And and_81 has open pins: In_1=u_matrix_controller_matriz_col[3], In_2=not_2_out[2], out=open
  // And and_82 has open pins: In_1=not_1_out[3], In_2=u_matrix_controller_matriz_col[3], out=open
  // And and_83 has open pins: In_1=not_3_out[3], In_2=u_matrix_controller_matriz_col[3], out=open
  // And and_84 has open pins: In_1=u_matrix_controller_matriz_col[3], In_2=not_2_out[3], out=open
  // And and_85 has open pins: In_1=not_1_out[4], In_2=u_matrix_controller_matriz_col[3], out=open
  // And and_86 has open pins: In_1=not_3_out[4], In_2=u_matrix_controller_matriz_col[3], out=open
  // And and_87 has open pins: In_1=u_matrix_controller_matriz_col[3], In_2=not_2_out[4], out=open
  // And and_88 has open pins: In_1=not_1_out[5], In_2=u_matrix_controller_matriz_col[3], out=open
  // And and_89 has open pins: In_1=not_3_out[5], In_2=u_matrix_controller_matriz_col[3], out=open
  // And and_90 has open pins: In_1=u_matrix_controller_matriz_col[3], In_2=not_2_out[5], out=open
  // And and_91 has open pins: In_1=not_1_out[6], In_2=u_matrix_controller_matriz_col[3], out=open
  // And and_92 has open pins: In_1=not_3_out[6], In_2=u_matrix_controller_matriz_col[3], out=open
  // And and_93 has open pins: In_1=u_matrix_controller_matriz_col[3], In_2=not_2_out[6], out=open
  // And and_94 has open pins: In_1=not_1_out[7], In_2=u_matrix_controller_matriz_col[3], out=open
  // And and_95 has open pins: In_1=not_3_out[7], In_2=u_matrix_controller_matriz_col[3], out=open
  // And and_96 has open pins: In_1=u_matrix_controller_matriz_col[3], In_2=not_2_out[7], out=open
  // RGBLED rgbled_25: pin names not known
  // RGBLED rgbled_26: pin names not known
  // RGBLED rgbled_27: pin names not known
  // RGBLED rgbled_28: pin names not known
  // RGBLED rgbled_29: pin names not known
  // RGBLED rgbled_30: pin names not known
  // RGBLED rgbled_31: pin names not known
  // RGBLED rgbled_32: pin names not known
  // And and_97 has open pins: In_1=not_1_out[0], In_2=u_matrix_controller_matriz_col[4], out=open
  // And and_98 has open pins: In_1=not_3_out[0], In_2=u_matrix_controller_matriz_col[4], out=open
  // And and_99 has open pins: In_1=u_matrix_controller_matriz_col[4], In_2=not_2_out[0], out=open
  // And and_100 has open pins: In_1=not_1_out[1], In_2=u_matrix_controller_matriz_col[4], out=open
  // And and_101 has open pins: In_1=not_3_out[1], In_2=u_matrix_controller_matriz_col[4], out=open
  // And and_102 has open pins: In_1=u_matrix_controller_matriz_col[4], In_2=not_2_out[1], out=open
  // And and_103 has open pins: In_1=not_1_out[2], In_2=u_matrix_controller_matriz_col[4], out=open
  // And and_104 has open pins: In_1=not_3_out[2], In_2=u_matrix_controller_matriz_col[4], out=open
  // And and_105 has open pins: In_1=u_matrix_controller_matriz_col[4], In_2=not_2_out[2], out=open
  // And and_106 has open pins: In_1=not_1_out[3], In_2=u_matrix_controller_matriz_col[4], out=open
  // And and_107 has open pins: In_1=not_3_out[3], In_2=u_matrix_controller_matriz_col[4], out=open
  // And and_108 has open pins: In_1=u_matrix_controller_matriz_col[4], In_2=not_2_out[3], out=open
  // And and_109 has open pins: In_1=not_1_out[4], In_2=u_matrix_controller_matriz_col[4], out=open
  // And and_110 has open pins: In_1=not_3_out[4], In_2=u_matrix_controller_matriz_col[4], out=open
  // And and_111 has open pins: In_1=u_matrix_controller_matriz_col[4], In_2=not_2_out[4], out=open
  // And and_112 has open pins: In_1=not_1_out[5], In_2=u_matrix_controller_matriz_col[4], out=open
  // And and_113 has open pins: In_1=not_3_out[5], In_2=u_matrix_controller_matriz_col[4], out=open
  // And and_114 has open pins: In_1=u_matrix_controller_matriz_col[4], In_2=not_2_out[5], out=open
  // And and_115 has open pins: In_1=not_1_out[6], In_2=u_matrix_controller_matriz_col[4], out=open
  // And and_116 has open pins: In_1=not_3_out[6], In_2=u_matrix_controller_matriz_col[4], out=open
  // And and_117 has open pins: In_1=u_matrix_controller_matriz_col[4], In_2=not_2_out[6], out=open
  // And and_118 has open pins: In_1=not_1_out[7], In_2=u_matrix_controller_matriz_col[4], out=open
  // And and_119 has open pins: In_1=not_3_out[7], In_2=u_matrix_controller_matriz_col[4], out=open
  // And and_120 has open pins: In_1=u_matrix_controller_matriz_col[4], In_2=not_2_out[7], out=open
  // RGBLED rgbled_33: pin names not known
  // RGBLED rgbled_34: pin names not known
  // RGBLED rgbled_35: pin names not known
  // RGBLED rgbled_36: pin names not known
  // RGBLED rgbled_37: pin names not known
  // RGBLED rgbled_38: pin names not known
  // RGBLED rgbled_39: pin names not known
  // RGBLED rgbled_40: pin names not known
  // And and_121 has open pins: In_1=not_1_out[0], In_2=u_matrix_controller_matriz_col[5], out=open
  // And and_122 has open pins: In_1=not_3_out[0], In_2=u_matrix_controller_matriz_col[5], out=open
  // And and_123 has open pins: In_1=u_matrix_controller_matriz_col[5], In_2=not_2_out[0], out=open
  // And and_124 has open pins: In_1=not_1_out[1], In_2=u_matrix_controller_matriz_col[5], out=open
  // And and_125 has open pins: In_1=not_3_out[1], In_2=u_matrix_controller_matriz_col[5], out=open
  // And and_126 has open pins: In_1=u_matrix_controller_matriz_col[5], In_2=not_2_out[1], out=open
  // And and_127 has open pins: In_1=not_1_out[2], In_2=u_matrix_controller_matriz_col[5], out=open
  // And and_128 has open pins: In_1=not_3_out[2], In_2=u_matrix_controller_matriz_col[5], out=open
  // And and_129 has open pins: In_1=u_matrix_controller_matriz_col[5], In_2=not_2_out[2], out=open
  // And and_130 has open pins: In_1=not_1_out[3], In_2=u_matrix_controller_matriz_col[5], out=open
  // And and_131 has open pins: In_1=not_3_out[3], In_2=u_matrix_controller_matriz_col[5], out=open
  // And and_132 has open pins: In_1=u_matrix_controller_matriz_col[5], In_2=not_2_out[3], out=open
  // And and_133 has open pins: In_1=not_1_out[4], In_2=u_matrix_controller_matriz_col[5], out=open
  // And and_134 has open pins: In_1=not_3_out[4], In_2=u_matrix_controller_matriz_col[5], out=open
  // And and_135 has open pins: In_1=u_matrix_controller_matriz_col[5], In_2=not_2_out[4], out=open
  // And and_136 has open pins: In_1=not_1_out[5], In_2=u_matrix_controller_matriz_col[5], out=open
  // And and_137 has open pins: In_1=not_3_out[5], In_2=u_matrix_controller_matriz_col[5], out=open
  // And and_138 has open pins: In_1=u_matrix_controller_matriz_col[5], In_2=not_2_out[5], out=open
  // And and_139 has open pins: In_1=not_1_out[6], In_2=u_matrix_controller_matriz_col[5], out=open
  // And and_140 has open pins: In_1=not_3_out[6], In_2=u_matrix_controller_matriz_col[5], out=open
  // And and_141 has open pins: In_1=u_matrix_controller_matriz_col[5], In_2=not_2_out[6], out=open
  // And and_142 has open pins: In_1=not_1_out[7], In_2=u_matrix_controller_matriz_col[5], out=open
  // And and_143 has open pins: In_1=not_3_out[7], In_2=u_matrix_controller_matriz_col[5], out=open
  // And and_144 has open pins: In_1=u_matrix_controller_matriz_col[5], In_2=not_2_out[7], out=open
  // RGBLED rgbled_41: pin names not known
  // RGBLED rgbled_42: pin names not known
  // RGBLED rgbled_43: pin names not known
  // RGBLED rgbled_44: pin names not known
  // RGBLED rgbled_45: pin names not known
  // RGBLED rgbled_46: pin names not known
  // RGBLED rgbled_47: pin names not known
  // RGBLED rgbled_48: pin names not known
  // And and_145 has open pins: In_1=not_1_out[0], In_2=u_matrix_controller_matriz_col[6], out=open
  // And and_146 has open pins: In_1=not_3_out[0], In_2=u_matrix_controller_matriz_col[6], out=open
  // And and_147 has open pins: In_1=u_matrix_controller_matriz_col[6], In_2=not_2_out[0], out=open
  // And and_148 has open pins: In_1=not_1_out[1], In_2=u_matrix_controller_matriz_col[6], out=open
  // And and_149 has open pins: In_1=not_3_out[1], In_2=u_matrix_controller_matriz_col[6], out=open
  // And and_150 has open pins: In_1=u_matrix_controller_matriz_col[6], In_2=not_2_out[1], out=open
  // And and_151 has open pins: In_1=not_1_out[2], In_2=u_matrix_controller_matriz_col[6], out=open
  // And and_152 has open pins: In_1=not_3_out[2], In_2=u_matrix_controller_matriz_col[6], out=open
  // And and_153 has open pins: In_1=u_matrix_controller_matriz_col[6], In_2=not_2_out[2], out=open
  // And and_154 has open pins: In_1=not_1_out[3], In_2=u_matrix_controller_matriz_col[6], out=open
  // And and_155 has open pins: In_1=not_3_out[3], In_2=u_matrix_controller_matriz_col[6], out=open
  // And and_156 has open pins: In_1=u_matrix_controller_matriz_col[6], In_2=not_2_out[3], out=open
  // And and_157 has open pins: In_1=not_1_out[4], In_2=u_matrix_controller_matriz_col[6], out=open
  // And and_158 has open pins: In_1=not_3_out[4], In_2=u_matrix_controller_matriz_col[6], out=open
  // And and_159 has open pins: In_1=u_matrix_controller_matriz_col[6], In_2=not_2_out[4], out=open
  // And and_160 has open pins: In_1=not_1_out[5], In_2=u_matrix_controller_matriz_col[6], out=open
  // And and_161 has open pins: In_1=not_3_out[5], In_2=u_matrix_controller_matriz_col[6], out=open
  // And and_162 has open pins: In_1=u_matrix_controller_matriz_col[6], In_2=not_2_out[5], out=open
  // And and_163 has open pins: In_1=not_1_out[6], In_2=u_matrix_controller_matriz_col[6], out=open
  // And and_164 has open pins: In_1=not_3_out[6], In_2=u_matrix_controller_matriz_col[6], out=open
  // And and_165 has open pins: In_1=u_matrix_controller_matriz_col[6], In_2=not_2_out[6], out=open
  // And and_166 has open pins: In_1=not_1_out[7], In_2=u_matrix_controller_matriz_col[6], out=open
  // And and_167 has open pins: In_1=not_3_out[7], In_2=u_matrix_controller_matriz_col[6], out=open
  // And and_168 has open pins: In_1=u_matrix_controller_matriz_col[6], In_2=not_2_out[7], out=open
  // RGBLED rgbled_49: pin names not known
  // RGBLED rgbled_50: pin names not known
  // RGBLED rgbled_51: pin names not known
  // RGBLED rgbled_52: pin names not known
  // RGBLED rgbled_53: pin names not known
  // RGBLED rgbled_54: pin names not known
  // RGBLED rgbled_55: pin names not known
  // RGBLED rgbled_56: pin names not known
  // And and_169 has open pins: In_1=not_1_out[0], In_2=u_matrix_controller_matriz_col[7], out=open
  // And and_170 has open pins: In_1=not_3_out[0], In_2=u_matrix_controller_matriz_col[7], out=open
  // And and_171 has open pins: In_1=u_matrix_controller_matriz_col[7], In_2=not_2_out[0], out=open
  // And and_172 has open pins: In_1=not_1_out[1], In_2=u_matrix_controller_matriz_col[7], out=open
  // And and_173 has open pins: In_1=not_3_out[1], In_2=u_matrix_controller_matriz_col[7], out=open
  // And and_174 has open pins: In_1=u_matrix_controller_matriz_col[7], In_2=not_2_out[1], out=open
  // And and_175 has open pins: In_1=not_1_out[2], In_2=u_matrix_controller_matriz_col[7], out=open
  // And and_176 has open pins: In_1=not_3_out[2], In_2=u_matrix_controller_matriz_col[7], out=open
  // And and_177 has open pins: In_1=u_matrix_controller_matriz_col[7], In_2=not_2_out[2], out=open
  // And and_178 has open pins: In_1=not_1_out[3], In_2=u_matrix_controller_matriz_col[7], out=open
  // And and_179 has open pins: In_1=not_3_out[3], In_2=u_matrix_controller_matriz_col[7], out=open
  // And and_180 has open pins: In_1=u_matrix_controller_matriz_col[7], In_2=not_2_out[3], out=open
  // And and_181 has open pins: In_1=not_1_out[4], In_2=u_matrix_controller_matriz_col[7], out=open
  // And and_182 has open pins: In_1=not_3_out[4], In_2=u_matrix_controller_matriz_col[7], out=open
  // And and_183 has open pins: In_1=u_matrix_controller_matriz_col[7], In_2=not_2_out[4], out=open
  // And and_184 has open pins: In_1=not_1_out[5], In_2=u_matrix_controller_matriz_col[7], out=open
  // And and_185 has open pins: In_1=not_3_out[5], In_2=u_matrix_controller_matriz_col[7], out=open
  // And and_186 has open pins: In_1=u_matrix_controller_matriz_col[7], In_2=not_2_out[5], out=open
  // And and_187 has open pins: In_1=not_1_out[6], In_2=u_matrix_controller_matriz_col[7], out=open
  // And and_188 has open pins: In_1=not_3_out[6], In_2=u_matrix_controller_matriz_col[7], out=open
  // And and_189 has open pins: In_1=u_matrix_controller_matriz_col[7], In_2=not_2_out[6], out=open
  // And and_190 has open pins: In_1=not_1_out[7], In_2=u_matrix_controller_matriz_col[7], out=open
  // And and_191 has open pins: In_1=not_3_out[7], In_2=u_matrix_controller_matriz_col[7], out=open
  // And and_192 has open pins: In_1=u_matrix_controller_matriz_col[7], In_2=not_2_out[7], out=open
  // RGBLED rgbled_57: pin names not known
  // RGBLED rgbled_58: pin names not known
  // RGBLED rgbled_59: pin names not known
  // RGBLED rgbled_60: pin names not known
  // RGBLED rgbled_61: pin names not known
  // RGBLED rgbled_62: pin names not known
  // RGBLED rgbled_63: pin names not known
  // RGBLED rgbled_64: pin names not known

  // Notes on the sheet:
  //   Clock_display: Hz: 5
endmodule

/* Code of matrix_controller:
module matrix_controller (
	input clock, display_refresh_clock, reset_display, show_display, desce_jogada,
	
	input [5:0] pontos,
	input [2:0] linhas_bloqueadas,
	input	[3:0] prox_jogada,
	
	output reg [7:0] matriz_col, matriz_r, matriz_g, matriz_b

);

	//  LINHAS					COLUNA RGB	**ATIVO BAIXO**
	reg [7:0] display_buffer [7:0][2:0];
	
	reg [7:0] jogadas [3:0];
	
	
	always @(posedge reset_display) begin
		jogadas[0] <= 8'b11111111;
		jogadas[1] <= 8'b11111111;
		jogadas[2] <= 8'b11111111;
		jogadas[3] <= 8'b11111111;
	end
	
	generate 
		genvar i;
		for (i = 0; i < 8; i=i+1) begin : ResetBuffer
			always @(posedge reset_display) begin
				display_buffer[i][0] <= 8'b11111111;
				display_buffer[i][1] <= 8'b11111111;
				display_buffer[i][2] <= 8'b11111111;
			end
		end
	endgenerate
	
	
	wire [7:0] line_block_mask;
	
	assign line_block_mask = ~(8'b11111111 >> linhas_bloqueadas);
	
	always @(posedge clock) begin
	
		if (desce_jogada) begin
			jogadas[0] <= {jogadas[0][6:0], ~prox_jogada[0]};
			jogadas[1] <= {jogadas[1][6:0], ~prox_jogada[1]};
			jogadas[2] <= {jogadas[2][6:0], ~prox_jogada[2]};
			jogadas[3] <= {jogadas[3][6:0], ~prox_jogada[3]};
		end
		
		display_buffer[2][0] <= jogadas[0] | line_block_mask;
		display_buffer[2][1] <= 8'b11111111 & (~line_block_mask);
		display_buffer[2][2] <= 8'b11111111 & (~line_block_mask);
		
		display_buffer[3][0] <= 8'b11111111;
		display_buffer[3][1] <= (jogadas[1] | line_block_mask) & (~line_block_mask);;
		display_buffer[3][2] <= 8'b11111111 & (~line_block_mask);
		
		display_buffer[4][0] <= 8'b11111111;
		display_buffer[4][1] <= 8'b11111111 & (~line_block_mask);
		display_buffer[4][2] <= (jogadas[2] | line_block_mask) & (~line_block_mask);;
		
		display_buffer[5][0] <= jogadas[3] | line_block_mask;
		display_buffer[5][1] <= (jogadas[3] | line_block_mask) & (~line_block_mask);;
		display_buffer[5][2] <= 8'b11111111 & (~line_block_mask);
		
		
		
		{display_buffer[7][0], display_buffer[6][0], display_buffer[1][0], display_buffer[0][0]} <= 32'hFFFFFFFF << pontos;
		{display_buffer[7][2], display_buffer[6][2], display_buffer[1][2], display_buffer[0][2]} <= 32'hFFFFFFFF << pontos;
		
	end
	
	
	wire [2:0] selected_col;
	
	contador_m #(.M(8), .N(3)) col_selector (
		.clock(display_refresh_clock),
		.zera_as(reset_display),
		.zera_s(1'b0),
		.conta(show_display),
		.Q(selected_col),
		.fim(),
		.meio()
	);
	
	always @(selected_col) begin
	
		case (selected_col) 
			3'b000: begin
				matriz_col 	<= 8'b00000001;
				matriz_r 	<= display_buffer[0][0];
				matriz_g 	<= display_buffer[0][1];
				matriz_b 	<= display_buffer[0][2];
			end
			3'b001: begin
				matriz_col 	<= 8'b00000010;
				matriz_r 	<= display_buffer[1][0];
				matriz_g 	<= display_buffer[1][1];
				matriz_b 	<= display_buffer[1][2];
			end
			3'b010: begin
				matriz_col 	<= 8'b00000100;
				matriz_r 	<= display_buffer[2][0];
				matriz_g 	<= display_buffer[2][1];
				matriz_b 	<= display_buffer[2][2];
			end
			3'b011: begin
				matriz_col 	<= 8'b00001000;
				matriz_r 	<= display_buffer[3][0];
				matriz_g 	<= display_buffer[3][1];
				matriz_b 	<= display_buffer[3][2];
			end
			3'b100: begin
				matriz_col 	<= 8'b00010000;
				matriz_r 	<= display_buffer[4][0];
				matriz_g 	<= display_buffer[4][1];
				matriz_b 	<= display_buffer[4][2];
			end
			3'b101: begin
				matriz_col 	<= 8'b00100000;
				matriz_r 	<= display_buffer[5][0];
				matriz_g 	<= display_buffer[5][1];
				matriz_b 	<= display_buffer[5][2];
			end
			3'b110: begin
				matriz_col 	<= 8'b01000000;
				matriz_r 	<= display_buffer[6][0];
				matriz_g 	<= display_buffer[6][1];
				matriz_b 	<= display_buffer[6][2];
			end
			3'b111: begin
				matriz_col 	<= 8'b10000000;
				matriz_r 	<= display_buffer[7][0];
				matriz_g 	<= display_buffer[7][1];
				matriz_b 	<= display_buffer[7][2];
			end
		endcase
	
	end

	

endmodule

module contador_m #(parameter M=100, N=7)
  (
   input  wire          clock,
   input  wire          zera_as,
   input  wire          zera_s,
   input  wire          conta,
   output reg  [N-1:0]  Q,
   output reg           fim,
   output reg           meio    
  );

  always @(posedge clock or posedge zera_as) begin
    if (zera_as) begin
      Q <= 0;
    end else if (clock) begin
      if (zera_s) begin
        Q <= 0;
      end else if (conta) begin
        if (Q == M-1) begin
          Q <= 0;
        end else begin
          Q <= Q + 1'b1;
        end
      end
    end
  end

  // Saidas
  always @ (Q)
      if (Q == M-1)   fim = 1;
      else            fim = 0;

  always @ (Q)
      if (Q == M/2-1) meio = 1;
      else            meio = 0;

endmodule
*/
